# Fritzing sketch FinalProj (saved by Fritzing 1.0.4)
breadboards: 1

parts:
  S3 = Pushbutton [package="[THT]"]
  S4 = Pushbutton [package="[THT]"]
  LED2 = LED - 5mm [color="Red (633nm)" current=0.030A package="5 mm [THT]"]
  LED4 = LED - 5mm [color="Blue (470nm)" current=0.030A package="5 mm [THT]"]
  LED5 = LED - 5mm [color="Yellow (585nm)" current=0.030A package="5 mm [THT]"]
  R1 = TRIMPOT [maximum_resistance=10kΩ knob_status=0% power=0.5W package=3362u-2]
  S2 = Pushbutton [package="[THT]"]
  R3 = Resistor [tolerance=±5% resistance=220 package="1206 [SMD]"]
  R4 = Resistor [tolerance=±5% resistance=220 package="1206 [SMD]"]
  R5 = Resistor [tolerance=±5% resistance=220 package="1206 [SMD]"]
  CPU2 = NodeMCU WROOM ESP 32  # not connected
  Mod1 = ESP32-TTGO-T-DISPLAY

nets:
  N1: S3.Pin_1, S3.Pin_2, Mod1.12
  N2: S3.Pin_3, S3.Pin_4, S4.Pin_3, S4.Pin_4, R1.CW, S2.Pin_3, S2.Pin_4, R3.Pin_0, R4.Pin_0, R5.Pin_0, Mod1.G-1, Mod1.G-2, Mod1.G-10, Mod1.G-11, Mod1.G-14
  N3: S4.Pin_1, S4.Pin_2, Mod1.32
  N4: LED2.cathode, R3.Pin_1
  N5: LED2.anode, Mod1.26
  N6: LED4.cathode, R4.Pin_1
  N7: LED4.anode, Mod1.2
  N8: LED5.cathode, R5.Pin_1
  N9: LED5.anode, Mod1.22
  N10: R1.CCW, Mod1.3V
  N11: R1.WIPER, Mod1.36
  N12: S2.Pin_1, S2.Pin_2, Mod1.13

custom parts:
  NodeMCU WROOM ESP 32: 30 pol Development Kit
  ESP32-TTGO-T-DISPLAY: LILYGO TTGO T-Display GD32VF103CBT6 Main Chip ST7789 1.14 Inch IPS 240x135 Resolution Minimalist Development Board.
